# Fritzing sketch TankSchematic (saved by Fritzing 0.9.3b)
perfboards: 2

parts:
  Part1 = Arduino Mega 2560 (Rev3)
  MD03A1 = Dual VNH2SP30 Motor Driver [part_number=MD03A]
  Part4 = Logic Level Converter
  M1 = DC Motor
  M2 = DC Motor
  U1 = LIPO-110mAh [package=lipo-110]
  U3 = LIPO-110mAh [package=lipo-110]
  U4 = LIPO-110mAh [package=lipo-110]
  J1 = Basic Servo
  J2 = Basic Servo
  Part5 = 10-DOF IMU L3GD20H + LSM303 + BMP180 [part_number=1604]
  U5 = NodeMCU V3.0
  C1 = Electrolytic Capacitor [capacitance=1µF package="100 mil [THT, electrolytic]"]
  Part6 = Bluetooth HC-05 Macho
  J4 = female pin header, 6 pins [form="♀ (female)"]
  J3 = female pin header, 11 pins [form="♀ (female)"]
  J5 = female pin header, 3 pins [form="♀ (female)"]
  J6 = female pin header, 3 pins [form="♀ (female)"]
  J7 = female pin header, 4 pins [form="♀ (female)"]

nets:
  N1: Part1.A0, MD03A1.1CS
  N2: Part1.A1, MD03A1.2CS
  N3: Part1.D21/SCL, Part5.SCL
  N4: Part1.D20/SDA, Part5.SDA
  GND: Part1.GND, MD03A1.GND#136, Part5.GND, J7.pin1
  N5: Part1.D9_PWM, J7.pin4
  N6: Part1.D8_PWM, J7.pin3
  N7: Part1.RESET, C1.+, J3.pin5
  5V: Part1.5V, MD03A1.+5V_(IN), Part5.VIN, J7.pin2
  N8: Part1.VIN, MD03A1.VIN#139
  N9: Part1.D0_RX0, Part4.TX_HV, J3.pin6
  N10: Part1.D1_TX0, Part4.RX_HV, J3.pin7
  N11: Part1.D3_PWM, MD03A1.PWM
  N12: Part1.D5_PWM, MD03A1.2PWM
  N13: Part1.D30, MD03A1.1DIAG/EN
  N14: Part1.D31, MD03A1.2DIAG/EN
  N15: Part1.D32, MD03A1.1INa
  N16: Part1.D33, MD03A1.2INb#142
  N17: Part1.D34, MD03A1.1INb
  N18: Part1.D35, MD03A1.2INb#143
  N19: MD03A1.OUT_1A, M2.pin_1
  N20: MD03A1.OUT_1B, M2.pin_2
  N21: MD03A1.OUT_2A, M1.pin_1
  N22: MD03A1.OUT_2B, M1.pin_2
  N23: MD03A1.VIN#150, U4.+
  N24: MD03A1.GND#151, U1.-
  N25: Part4.TX2_LV, U5.D6
  N26: Part4.RX2_LV, U5.D5
  N27: Part4.GND, U5.GND#6, U5.GND#13, U5.GND#16, U5.GND#33
  N28: Part4.LV, U5.3V3
  N29: Part4.RX_LV, Part6.TXD, J4.pin4
  N30: Part4.TX_LV, Part6.RXD, J4.pin5
  N31: Part4.RX2_HV, J3.pin10
  N32: Part4.TX2_HV, J3.pin11
  N33: U1.+, U3.-
  N34: U3.+, U4.-
  N35: J1.gnd, J5.pin1
  N36: J1.vcc, J5.pin2
  N37: J1.pulse, J5.pin3
  N38: J2.gnd, J6.pin1
  N39: J2.vcc, J6.pin2
  N40: J2.pulse, J6.pin3
  N41: C1.-, Part6.State, J4.pin6
  N42: Part6.VCC, J4.pin2, J3.pin8
  N43: Part6.Key, J4.pin1
  N44: Part6.GND, J4.pin3, J3.pin9

custom parts:
  10-DOF IMU L3GD20H + LSM303 + BMP180: This inertial-measurement-unit combines 3 of the best quality sensors available on the market to give you 11 axes of data: 3 axes of accelerometer data, 3 axes gyroscopic, 3 axes magnetic (compass), barometric pressure/altitude and temperature. We tested many different 'combination' sensors and found these were the best value, with stable and reliable readings.
  NodeMCU V3.0: ESP8266 based NodeMCU
